# Fritzing sketch Blink_Blasic (saved by Fritzing 0.9.3b)
breadboards: 1

parts:
  LED2 = LED - 5mm [color="Red (633nm)" package="5 mm [THT]"]
  Part1 = Arduino Uno (Rev3)
  R1 = Resistor [tolerance=±5% resistance=220 package="1206 [SMD]"]

nets:
  N1: LED2.cathode, Part1.GND
  N2: LED2.anode, R1.Pin_0
  N3: Part1.D8, R1.Pin_1

notes:
  LED
  Breadboard
  Arduino

// code stored in the sketch: Blink_LED.ino
int ledPin = 8;

void setup(){
	pinMode(ledPin,OUTPUT);
	serial.begin(9600);
}

void loop(){
	digitalWrite(ledPin,HIGH);
	Serial.println(ledPin);
	delay(2000);
	digitalWrite(ledPin,LOW);
	delay(2000);
}
