# Fritzing sketch Ultrasonic _Sensor_with_Arduino (saved by Fritzing 0.9.3b)
breadboards: 1

parts:
  Part1 = Arduino Uno (Rev3)
  hc-sr1 = hc-sr04
  LED1 = LED - 5mm [color="Red (633nm)" package="5 mm [THT]"]

nets:
  N1: Part1.D8, hc-sr1.Echo
  N2: Part1.D9_PWM, hc-sr1.Trig
  N3: Part1.D7, LED1.anode
  5V: Part1.5V, hc-sr1.VCC
  GND: Part1.GND, hc-sr1.GND, LED1.cathode

notes:
  Ultrasonic Sensor
  Breadboard
  Arduino
  LED
